# Fritzing sketch L298 (saved by Fritzing 0.9.4)

parts:
  Part1 = Arduino Uno (Rev3)
  VCC1 = Battery block 9V
  M1 = DC Motor
  S1 = H-Bridge with L298N

nets:
  N1: Part1.D8, S1.IN2
  N2: Part1.D9_PWM, S1.IN1
  N3: Part1.D10_PWM/SS, S1.ENA
  GND: Part1.GND, VCC1.-, S1.GND
  N4: VCC1.+, S1.12V
  N5: M1.pin_1, S1.M1-02

custom parts:
  H-Bridge with L298N: h-bridge
